# Fritzing sketch buzzer (saved by Fritzing 0.9.3b)
breadboards: 1

parts:
  Урок_10 = Arduino Uno (Rev3)
  R1 = Photocell (LDR) [package=THT]
  J1 = Piezo Speaker
  R2 = Resistor [tolerance=±5% resistance=10k package=THT]

nets:
  N1: Урок_10.A0, R1.pin_1, R2.Pin_1
  N2: Урок_10.D3_PWM, J1.pin2
  N3: Урок_10.5V, R2.Pin_0
  N4: Урок_10.GND, R1.pin_0, J1.pin1
