# Fritzing sketch motor (saved by Fritzing 0.9.3b)
breadboards: 1

parts:
  Урок_12 = Arduino Nano (Rev3.0)
  Часть4 = Pololu 3.3V Step-Up Voltage Regulator U1V11F3
  Часть5 = Pololu 3.3V Step-Up Voltage Regulator U1V11F3
  Driver = DRV8835 Dual Motor Driver Carrier

nets:
  GND: Урок_12.GND, Driver.GND
  N1: Урок_12.D7, Driver.BIN1/BPHASE
  N2: Урок_12.D8, Driver.AIN1/APHASE
  N3: Урок_12.D9, Часть4.IN1, Driver.BIN2/BENABLE, Driver.AOUT1
  N4: Урок_12.D10, Driver.AIN2/AENABLE
  5V: Урок_12.5V, Driver.VCC, Driver.MODE, Driver.VIN
  N5: Часть4.IN2, Driver.AOUT2
  N6: Часть5.IN1, Driver.BOUT1
  N7: Часть5.IN2, Driver.BOUT2
