# Fritzing sketch keyboard_pcb (saved by Fritzing 0.9.3b)
breadboards: 1

parts:
  Часть1 = Arduino Uno (Rev3)
  Keypad4x1 = Keypad Membran 4x4
  J1 = Piezo Speaker

nets:
  N1: Часть1.D8, Keypad4x1.Pin2
  N2: Часть1.D9_PWM, Keypad4x1.Pin1
  N3: Часть1.D10_PWM/SS, J1.pin1
  N4: Часть1.D2, Keypad4x1.Pin8
  N5: Часть1.D3_PWM, Keypad4x1.Pin7
  N6: Часть1.D4, Keypad4x1.Pin6
  N7: Часть1.D5_PWM, Keypad4x1.Pin5
  N8: Часть1.D6_PWM, Keypad4x1.Pin4
  N9: Часть1.D7, Keypad4x1.Pin3
  N10: Часть1.5V, J1.pin2

custom parts:
  Keypad Membran 4x4: Membrane Keypad 4x4 Matrix
