# Fritzing sketch joy (saved by Fritzing 0.9.3b)
breadboards: 1

parts:
  J1 = Basic Servo
  J2 = Basic Servo
  Часть1 = Arduino Uno (Rev3)
  Part2 = Thumb Joystick

nets:
  GND: J1.gnd, J2.gnd, Часть1.GND, Part2.GND
  VCC: J1.vcc, J2.vcc, Часть1.5V, Part2.VCC
  N1: Часть1.A0, Part2.VERT
  N2: Часть1.A1, Part2.HORZ
