# Fritzing sketch cap (saved by Fritzing 0.9.3b)
breadboards: 1

parts:
  Часть1 = Arduino Uno (Rev3)
  LED1 = LED - 5mm [color="Red (633nm)" package="5 mm [THT]"]
  R1 = Resistor [tolerance=±5% resistance=220 package=THT]
  R3 = Resistor [tolerance=±10% resistance=35k package=THT]
  R2 = Resistor [tolerance=±20% resistance=20k package=THT]

nets:
  N1: Часть1.D2, LED1.anode
  N2: Часть1.D3_PWM, R2.Pin_0
  N3: Часть1.D4, R3.Pin_1
  N4: Часть1.GND, R1.Pin_0
  N5: LED1.cathode, R1.Pin_1
  N6: R3.Pin_0, R2.Pin_1

notes:
  СЕНСОР
