# Fritzing sketch game_pcb (saved by Fritzing 0.9.3b)
breadboards: 1

parts:
  Часть1 = Arduino Uno (Rev3)
  S1 = Pushbutton [package="[THT]"]
  S2 = Pushbutton [package="[THT]"]
  S3 = Pushbutton [package="[THT]"]
  S4 = Pushbutton [package="[THT]"]
  OLED_I2C1 = OLED 128x64 I2C Monochrome Display

nets:
  N1: Часть1.A0, S4.Pin_1, S4.Pin_2
  N2: Часть1.A1, S3.Pin_1, S3.Pin_2
  N3: Часть1.A2, S2.Pin_3, S2.Pin_4
  N4: Часть1.A3, S1.Pin_3, S1.Pin_4
  N5: Часть1.A4/SDA, OLED_I2C1.SDA
  N6: Часть1.A5/SCL, OLED_I2C1.SCK
  5V: Часть1.5V, OLED_I2C1.VDD
  GND: Часть1.GND, S1.Pin_1, S1.Pin_2, S2.Pin_1, S2.Pin_2, S3.Pin_3, S3.Pin_4, S4.Pin_3, S4.Pin_4, OLED_I2C1.GND
