# Fritzing sketch shift_pcb (saved by Fritzing 0.9.3b)
breadboards: 1

parts:
  Часть1 = Arduino Uno (Rev3)
  7_Segment1 = 7-Segment LED Display [package=THT]
  U1 = 74HC595 [package="DIP16 [THT]"]
  R1 = Resistor [tolerance=±20% resistance=220 package=THT]
  R2 = Resistor [tolerance=±20% resistance=220 package=THT]
  R3 = Resistor [tolerance=±20% resistance=220 package=THT]
  R4 = Resistor [tolerance=±5% resistance=220 package=THT]
  R5 = Resistor [tolerance=±5% resistance=220 package=THT]
  R6 = Resistor [tolerance=±5% resistance=220 package=THT]
  R7 = Resistor [tolerance=±5% resistance=220 package=THT]

nets:
  N1: Часть1.D11_PWM/MOSI, U1.DS
  N2: Часть1.D12/MISO, U1.SH_CP
  N3: Часть1.D13/SCK, U1.ST_CP
  5V: Часть1.5V, U1.MR, U1.VCC
  GND: Часть1.GND, 7_Segment1.commAnode#7, U1.GND, U1.OE
  N4: 7_Segment1.cathodeE, R1.Pin_1
  N5: 7_Segment1.cathodeD, R2.Pin_1
  N6: 7_Segment1.cathodeC, R3.Pin_1
  N7: 7_Segment1.cathodeB, R7.Pin_0
  N8: 7_Segment1.cathodeA, R6.Pin_0
  N9: 7_Segment1.cathodeF, R5.Pin_0
  N10: 7_Segment1.cathodeG, R4.Pin_0
  N11: U1.Q1, R1.Pin_0
  N12: U1.Q2, R2.Pin_0
  N13: U1.Q3, R3.Pin_0
  N14: U1.Q4, R4.Pin_1
  N15: U1.Q5, R5.Pin_1
  N16: U1.Q6, R6.Pin_1
  N17: U1.Q7, R7.Pin_1
