# Fritzing sketch POV (saved by Fritzing 0.9.3b)
circuit board: 7cm x 6cm

parts:
  Часть1 = Arduino Nano (Rev3.0)
  R1 = Resistor [tolerance=±5% resistance=220 package=THT]
  R2 = Resistor [tolerance=±5% resistance=220 package=THT]
  R3 = Resistor [tolerance=±5% resistance=220 package=THT]
  R4 = Resistor [tolerance=±5% resistance=220 package=THT]
  R5 = Resistor [tolerance=±5% resistance=220 package=THT]
  R6 = Resistor [tolerance=±5% resistance=220 package=THT]
  R7 = Resistor [tolerance=±5% resistance=220 package=THT]
  R8 = Resistor [tolerance=±5% resistance=220 package=THT]
  LED1 = LED - 5mm [color="Red (633nm)" package="5 mm [THT]"]
  LED2 = LED - 5mm [color="Red (633nm)" package="5 mm [THT]"]
  LED3 = LED - 5mm [color="Red (633nm)" package="5 mm [THT]"]
  LED5 = LED - 5mm [color="Red (633nm)" package="5 mm [THT]"]
  LED6 = LED - 5mm [color="Red (633nm)" package="5 mm [THT]"]
  LED7 = LED - 5mm [color="Red (633nm)" package="5 mm [THT]"]
  LED8 = LED - 5mm [color="Red (633nm)" package="5 mm [THT]"]
  S2 = Pushbutton [package="[THT]"]
  S1 = Pushbutton [package="[THT]"]
  BAT1 = BC9VPC [package=bc9vpc]
  LED4 = LED - 5mm [color="Red (633nm)" package="5 mm [THT]"]

nets:
  N1: Часть1.GND, LED1.cathode, LED2.cathode, LED3.cathode, LED5.cathode, LED6.cathode, LED7.cathode, LED8.cathode, S2.Pin_3, S2.Pin_4, S1.Pin_3, S1.Pin_4, BAT1.V-, LED4.cathode
  N2: Часть1.D2, S1.Pin_1, S1.Pin_2
  N3: Часть1.D3, S2.Pin_1, S2.Pin_2
  N4: Часть1.D9, R8.Pin_0
  N5: Часть1.D10, R7.Pin_0
  N6: Часть1.D11/MOSI, R6.Pin_0
  N7: Часть1.D12/MISO, R5.Pin_0
  N8: Часть1.VIN, BAT1.V+
  N9: Часть1.A3, R1.Pin_0
  N10: Часть1.A2, R2.Pin_0
  N11: Часть1.A1, R3.Pin_0
  N12: Часть1.A0, R4.Pin_0
  N13: R1.Pin_1, LED1.anode
  N14: R2.Pin_1, LED2.anode
  N15: R3.Pin_1, LED3.anode
  N16: R4.Pin_1, LED4.anode
  N17: R5.Pin_1, LED5.anode
  N18: R6.Pin_1, LED6.anode
  N19: R7.Pin_1, LED7.anode
  N20: R8.Pin_1, LED8.anode
