# Fritzing sketch Semafore_pcb (saved by Fritzing 0.9.3b)
breadboards: 2

parts:
  Часть1 = Arduino Nano (Rev3.0)
  LED1 = LED - 5mm [color="Red (633nm)" package="5 mm [THT]"]
  LED2 = LED - 5mm [color="Yellow (595nm)" package="5 mm [THT]"]
  LED3 = LED - 5mm [color="Green (555nm)" package="5 mm [THT]"]
  R1 = Resistor [tolerance=±5% resistance=220 package=THT]
  R2 = Resistor [tolerance=±5% resistance=220 package=THT]
  R3 = Resistor [tolerance=±5% resistance=220 package=THT]
  S1 = Pushbutton [package="[THT]"]
  Часть2 = Arduino Nano (Rev3.0)
  LED4 = LED - 5mm [color="Red (633nm)" package="5 mm [THT]"]
  R6 = Resistor [tolerance=±5% resistance=220 package=THT]

nets:
  N1: Часть1.GND, LED1.cathode, LED2.cathode, LED3.cathode, S1.Pin_1, S1.Pin_2
  N2: Часть1.A3, S1.Pin_3, S1.Pin_4
  N3: Часть1.A2, R3.Pin_1
  N4: Часть1.A1, R2.Pin_1
  N5: Часть1.A0, R1.Pin_1
  N6: LED1.anode, R1.Pin_0
  N7: LED2.anode, R2.Pin_0
  N8: LED3.anode, R3.Pin_0
  N9: Часть2.GND, LED4.cathode
  N10: Часть2.A0, R6.Pin_1
  N11: LED4.anode, R6.Pin_0
