# Fritzing sketch lession6 (saved by Fritzing 0.9.3b)
breadboards: 1

parts:
  Урок_6 = Arduino Uno (Rev3)
  Светодиод = LED - 5mm [color="Red (633nm)" package="5 mm [THT]"]
  R1 = Resistor [tolerance=±5% resistance=220 package=THT]
  Inf = LED - 5mm [color="White (4500K)" package="5 mm [THT]"]
  R2 = Resistor [tolerance=±5% resistance=10k package=THT]
  Inf_приемник = LED - 5mm [color="Infrared (940nm)" package="5 mm [THT]"]

nets:
  N1: Урок_6.A0, R2.Pin_1, Inf_приемник.cathode
  N2: Урок_6.D2, Светодиод.anode
  N3: Урок_6.D3_PWM, Inf.anode
  N4: Урок_6.5V, R2.Pin_0
  N5: Урок_6.GND, R1.Pin_1, Inf.cathode, Inf_приемник.anode
  N6: Светодиод.cathode, R1.Pin_0
