# Fritzing sketch lcd_pcb (saved by Fritzing 0.9.3b)
breadboards: 1

parts:
  LCD1 = LCD screen
  Часть1 = Arduino Uno (Rev3)
  R1 = Rotary Potentiometer (Small) [maximum_resistance=100kΩ package=THT]

nets:
  VSS: LCD1.VSS, LCD1.R/W, LCD1.LED-, Часть1.GND, R1.wiper
  VDD: LCD1.VDD, LCD1.LED+, Часть1.5V
  N1: LCD1.V0, R1.leg1
  N2: LCD1.RS, Часть1.D4
  N3: LCD1.E, Часть1.D5_PWM
  N4: LCD1.DB4, Часть1.D10_PWM/SS
  N5: LCD1.DB5, Часть1.D11_PWM/MOSI
  N6: LCD1.DB6, Часть1.D12/MISO
  N7: LCD1.DB7, Часть1.D13/SCK
