# Fritzing sketch motor_pcb (saved by Fritzing 0.9.3b)
breadboards: 1

parts:
  Часть1 = Arduino Uno (Rev3)
  M1 = DC Motor
  R1 = Resistor [tolerance=±5% resistance=10k package=THT]
  R2 = Resistor [tolerance=±5% resistance=220 package=THT]
  Q1 = Basic FET P-Channel [package="TO220 [THT]"]

nets:
  N1: Часть1.D3_PWM, R2.Pin_0
  N2: Часть1.5V, M1.pin_2
  N3: Часть1.GND, R1.Pin_1, Q1.source
  N4: M1.pin_1, Q1.drain
  N5: R1.Pin_0, R2.Pin_1, Q1.gate
